# Fritzing sketch Arduino Mega2560  DD20Emu (saved by Fritzing 0.9.4)

parts:
  Part1 = Arduino Ethernet Shield (Rev3)
  DD20_Connector = shrouded pin header, 20 pins [form="♂ (shrouded male)"]
  Part2 = Arduino Mega 2560 (Rev3)

nets:
  N1: Part1.D2, DD20_Connector.pin16
  N2: Part1.PWM_D3, DD20_Connector.pin14
  N3: Part1.SDCS, DD20_Connector.pin13
  N4: Part1.PWM_D5, DD20_Connector.pin12
  N5: Part1.PWM_D6, DD20_Connector.pin11
  N6: Part1.D7, DD20_Connector.pin15
  N7: DD20_Connector.pin1, Part2.GND
  N8: DD20_Connector.pin17, Part2.A11
  N9: DD20_Connector.pin18, Part2.A10
  N10: DD20_Connector.pin19, Part2.A9
  N11: DD20_Connector.pin20, Part2.A8

notes:
  Gnd
  RD DATA
  /Enable
  /WReq
  Step0
  Step1
  Step2
  Step3
  DD20 Conn
  WR DATA
  WR PROT
  Emulator enable
