# Fritzing sketch Arduino UNO DD20Emu (saved by Fritzing 0.9.4)

parts:
  Part1 = Arduino Ethernet Shield (Rev3)
  Part2 = Arduino Uno (Rev3)  # not connected
  DD20_Connector = shrouded pin header, 20 pins [form="♂ (shrouded male)"]

nets:
  N1: Part1.A0, DD20_Connector.pin20
  N2: Part1.A1, DD20_Connector.pin19
  N3: Part1.A2, DD20_Connector.pin18
  N4: Part1.A3, DD20_Connector.pin17
  N5: Part1.D2, DD20_Connector.pin16
  N6: Part1.PWM_D3, DD20_Connector.pin14
  N7: Part1.SDCS, DD20_Connector.pin13
  N8: Part1.PWM_D5, DD20_Connector.pin12
  N9: Part1.PWM_D6, DD20_Connector.pin11
  N10: Part1.D7, DD20_Connector.pin15
  N11: Part1.GND, DD20_Connector.pin1

notes:
  Gnd
  RD DATA
  /Enable
  /WReq
  Step0
  Step1
  Step2
  Step3
  DD20 Conn
  WR DATA
  WR PROT
  Emulator enable
